# Fritzing sketch schematic_perfboard (saved by Fritzing 1.0.2b)
perfboards: 1

parts:
  U1 = 2-Channel 5v Relay Shield [package=relay-2ch5v10a]
  Bauteil1 = I2C level shifter bidirectional
  R1 = Resistor [tolerance=±5% resistance=22k package="1206 [SMD]"]
  R2 = Resistor [tolerance=±5% resistance=100k package="1206 [SMD]"]
  C1 = Electrolytic Capacitor [capacitance=1µF voltage=35V package="100 mil [THT, electrolytic]"]  # not connected
  C2 = Tantalum Capacitor [capacitance="1 μF" voltage=35V package="A 3216 [SMD, tantalum]"]  # not connected
  TP1 = TP4056 [chip_label=TP4056 package="DIP (Dual Inline) [THT]"]
  Q1 = PNP-Transistor [package="TO92 [THT]"]
  J3 = female pin header, 4 pins [form="♀ (female)"]
  Mod1 = Amica NodeMCU DEVKIT 1.0
  J4 = female pin header, 2 pins [form="♀ (female)"]
  J5 = female pin header, 3 pins [form="♀ (female)"]
  J9 = female pin header, 2 pins [form="♀ (female)"]
  J10 = female pin header, 3 pins [form="♀ (female)"]
  Capacitive_Soil_Moisture_Sensor1 = DFRobot Capacitive Soil Moisture Sensor V1.0 [part_number=SEN0193]
  J11 = female pin header, 2 pins [form="♀ (female)"]
  J12 = female pin header, 2 pins [form="♀ (female)"]
  J13 = female pin header, 2 pins [form="♀ (female)"]
  J14 = female pin header, 2 pins [form="♀ (female)"]

nets:
  N1: U1.VCC, Bauteil1.HV, J3.pin1
  N2: U1.GND, J3.pin4
  N3: U1.IN1, Bauteil1.HV4, J3.pin3
  N4: U1.IN2, Bauteil1.HV3, J3.pin2
  N5: U1.K1-In, J9.pin2
  N6: U1.K1-On, J12.pin2, J14.pin1
  N7: U1.K2-In, J9.pin1
  N8: U1.K2-On, J13.pin1, J14.pin2
  N9: Bauteil1.LV4, Mod1.pin_28
  N10: Bauteil1.LV3, Mod1.pin_27
  N11: Bauteil1.GND, J12.pin1
  N12: R1.Pin_1, TP1.pin3, Q1.C
  N13: R2.Pin_0, Mod1.pin_21
  N14: TP1.pin1, J11.pin1
  N15: TP1.pin2, J11.pin2
  N16: TP1.pin4, J4.pin2
  N17: TP1.pin5, J4.pin1
  N18: TP1.pin6, Mod1.pin2, Mod1.pin_9, Mod1.pin_25, Mod1.pin_29, J5.pin1, J10.pin1, Capacitive_Soil_Moisture_Sensor1.GND
  N19: Q1.B, Mod1.pin1, Mod1.pin_10, Mod1.pin_26, J5.pin2, Capacitive_Soil_Moisture_Sensor1.VCC
  N20: Mod1.pin_19, J10.pin3
  N21: Mod1.pin_20, J5.pin3, Capacitive_Soil_Moisture_Sensor1.A

custom parts:
  2-Channel 5v Relay Shield: 2 Channel 5v Relay Shield w. 2x SPD-06VDC-SD-C
  TP4056: A DIP stand-in part for whatever IC you want. With 6 pins on a 300mil dual inline package (DIP) footprint.
  DFRobot Capacitive Soil Moisture Sensor V1.0: DFRobot Capacitive Soil Moisture Sensor V1.0 This product measures soil moisture levels by capacitive sensing, rather than resistive sensing like other types of moisture sensor. It is made of a corrosion resistant material giving it a long service life. Insert it into soil and impress your friends with the real-time soil moisture data! The product includes an on-board voltage regulator which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
